# Fritzing sketch LED-Netz_halb (saved by Fritzing 0.9.4)
circuit board: 8.46667cm x 5.64444cm
breadboards: 1

parts:
  IC2 = DIP - 16 pins [chip_label=74HC138 package="DIP (Dual Inline) [THT]"]
  IC1 = DIP - 16 pins [chip_label=74HC138 package="DIP (Dual Inline) [THT]"]
  J1 = Camdenboss CTB0158-3 [part_number=CTB0158-3 package=THT]
  J2 = Camdenboss CTB0158-2 [part_number=CTB0158-3 package=THT]
  Q1 = Basic FET P-Channel [package="DPak [SMD]"]
  Q2 = Basic FET P-Channel [package="DPak [SMD]"]
  Q3 = Basic FET P-Channel [package="DPak [SMD]"]
  IC3 = DIP - 16 pins [chip_label=74HC138 package="DIP (Dual Inline) [THT]"]
  IC4 = IC, DIP package, 24 pins [chip_label=TM1818]
  J4 = Camdenboss CTB0158-4 [part_number=CTB0158-4 package=THT]
  R1 = Resistor [tolerance=±5% resistance=620 package=THT]
  R2 = Resistor [tolerance=±5% resistance=620 package=THT]
  R3 = Resistor [tolerance=±5% resistance=33 package=THT]
  R4 = Resistor [tolerance=±5% resistance=33 package=THT]
  R5 = Resistor [tolerance=±5% resistance=33 package=THT]
  LED1 = LEDs [package=led10mm]
  LED2 = LEDs [package=led10mm]
  LED3 = LEDs [package=led10mm]
  LED4 = LEDs [package=led10mm]
  LED5 = LEDs [package=led10mm]
  LED6 = LEDs [package=led10mm]
  LED7 = LEDs [package=led10mm]
  LED8 = LEDs [package=led10mm]
  LED9 = LEDs [package=led10mm]
  R11 = Resistor [tolerance=±5% resistance=4.7k package=THT]
  R12 = Resistor [tolerance=±5% resistance=4.7k package=THT]
  R13 = Resistor [tolerance=±5% resistance=4.7k package=THT]
  R14 = Resistor [tolerance=±5% resistance=4.7k package=THT]
  R19 = Resistor [tolerance=±5% resistance=33 package=THT]
  R20 = Resistor [tolerance=±5% resistance=33 package=THT]
  R21 = Resistor [tolerance=±5% resistance=33 package=THT]
  LED19 = LEDs [package=led10mm]
  LED20 = LEDs [package=led10mm]
  LED21 = LEDs [package=led10mm]
  LED22 = LEDs [package=led10mm]
  LED23 = LEDs [package=led10mm]
  LED24 = LEDs [package=led10mm]
  LED25 = LEDs [package=led10mm]
  LED26 = LEDs [package=led10mm]
  LED27 = LEDs [package=led10mm]
  IC8 = IC, DIP package, 24 pins [chip_label=TM1818]

nets:
  N1: IC2.A0, IC1.A0, J1.pin3, IC3.A0
  N2: IC2.A1, IC1.A1, J1.pin2, IC3.A1
  N3: IC2.A2, IC1.A2, J1.pin1, IC3.A2
  GND: IC2.CS2, IC2.GND, IC1.GND, IC3.CS2, IC3.CS3, IC3.GND, IC4.pin1, R1.Pin_1, R2.Pin_1
  N4: IC2.CS3, IC1.CS3, J2.pin1, IC3.CS1
  N5: IC2.CS1, IC1.CS2, J2.pin2
  5V: IC2.VCC, IC1.CS1, IC1.VCC, Q1.source, Q2.source, Q3.source, IC3.VCC, IC4.pin24, R11.Pin_0, R12.Pin_0, R13.Pin_0, R14.Pin_0
  N6: IC1.Y2, Q3.Gate
  N7: IC1.Y1, Q2.Gate
  N8: IC1.Y0, Q1.Gate
  N9: Q1.drain, LED1.A, LED2.A, LED3.A, LED25.A, LED26.A, LED27.A
  N10: Q2.drain, LED4.A, LED5.A, LED6.A, LED22.A, LED23.A, LED24.A
  N11: Q3.drain, LED7.A, LED8.A, LED9.A, LED19.A, LED20.A, LED21.A
  N12: IC4.pin2, J4.pin3, R12.Pin_1
  N13: IC4.pin3, J4.pin2, R13.Pin_1, IC8.pin3
  N14: IC4.pin4, J4.pin1, R14.Pin_1, IC8.pin4
  N15: IC4.pin18, R5.Pin_1
  N16: IC4.pin19, R4.Pin_1
  N17: IC4.pin20, R3.Pin_1
  N18: IC4.pin21, J4.pin4, R11.Pin_1, IC8.pin21
  N19: IC4.pin22, IC8.pin2
  N20: IC4.pin23, R1.Pin_0
  N21: R2.Pin_0, IC8.pin23
  N22: R3.Pin_0, LED2.C, LED6.C, LED7.C
  N23: R4.Pin_0, LED1.C, LED5.C, LED8.C
  N24: R5.Pin_0, LED3.C, LED4.C, LED9.C
  N25: R19.Pin_0, LED19.C, LED24.C, LED25.C
  N26: R19.Pin_1, IC8.pin18
  N27: R20.Pin_0, LED20.C, LED23.C, LED27.C
  N28: R20.Pin_1, IC8.pin19
  N29: R21.Pin_0, LED21.C, LED22.C, LED26.C
  N30: R21.Pin_1, IC8.pin20
