# Fritzing sketch Lichternetz (saved by Fritzing 0.9.4)
circuit board: 8.46667cm x 5.64444cm
breadboards: 1

parts:
  IC2 = DIP - 16 pins [chip_label=74HC138 package="DIP (Dual Inline) [THT]"]
  IC1 = DIP - 16 pins [chip_label=74HC138 package="DIP (Dual Inline) [THT]"]
  J1 = Camdenboss CTB0158-3 [part_number=CTB0158-3 package=THT]
  J2 = Camdenboss CTB0158-2 [part_number=CTB0158-3 package=THT]
  Q1 = Basic FET P-Channel [package="DPak [SMD]"]
  Q2 = Basic FET P-Channel [package="DPak [SMD]"]
  Q3 = Basic FET P-Channel [package="DPak [SMD]"]
  IC3 = DIP - 16 pins [chip_label=74HC138 package="DIP (Dual Inline) [THT]"]
  IC4 = IC, DIP package, 24 pins [chip_label=TM1818]
  IC5 = DIP - 24 pins [chip_label=TM1818 package="DIP (Dual Inline) [THT]"]
  J4 = Camdenboss CTB0158-4 [part_number=CTB0158-4 package=THT]
  R1 = Resistor [tolerance=±5% resistance=620 package=THT]
  R2 = Resistor [tolerance=±5% resistance=620 package=THT]
  R3 = Resistor [tolerance=±5% resistance=33 package=THT]
  R4 = Resistor [tolerance=±5% resistance=33 package=THT]
  R5 = Resistor [tolerance=±5% resistance=33 package=THT]
  LED1 = LEDs [package=led10mm]
  LED2 = LEDs [package=led10mm]
  LED3 = LEDs [package=led10mm]
  LED4 = LEDs [package=led10mm]
  LED5 = LEDs [package=led10mm]
  LED6 = LEDs [package=led10mm]
  LED7 = LEDs [package=led10mm]
  LED8 = LEDs [package=led10mm]
  LED9 = LEDs [package=led10mm]
  IC6 = IC, DIP package, 24 pins [chip_label=TM1818]
  J5 = Camdenboss CTB0158-4 [part_number=CTB0158-4 package=THT]
  IC7 = DIP - 24 pins [chip_label=TM1818 package="DIP (Dual Inline) [THT]"]
  R6 = Resistor [tolerance=±5% resistance=620 package=THT]
  R7 = Resistor [tolerance=±5% resistance=620 package=THT]
  R8 = Resistor [tolerance=±5% resistance=33 package=THT]
  R9 = Resistor [tolerance=±5% resistance=33 package=THT]
  R10 = Resistor [tolerance=±5% resistance=33 package=THT]
  LED10 = LEDs [package=led10mm]
  LED11 = LEDs [package=led10mm]
  LED12 = LEDs [package=led10mm]
  LED13 = LEDs [package=led10mm]
  LED14 = LEDs [package=led10mm]
  LED15 = LEDs [package=led10mm]
  LED16 = LEDs [package=led10mm]
  LED17 = LEDs [package=led10mm]
  LED18 = LEDs [package=led10mm]
  R11 = Resistor [tolerance=±5% resistance=4.7k package=THT]
  R12 = Resistor [tolerance=±5% resistance=4.7k package=THT]
  R13 = Resistor [tolerance=±5% resistance=4.7k package=THT]
  R14 = Resistor [tolerance=±5% resistance=4.7k package=THT]
  R15 = Resistor [tolerance=±5% resistance=4.7k package=THT]
  R16 = Resistor [tolerance=±5% resistance=4.7k package=THT]
  R17 = Resistor [tolerance=±5% resistance=4.7k package=THT]
  R18 = Resistor [tolerance=±5% resistance=4.7k package=THT]
  R19 = Resistor [tolerance=±5% resistance=33 package=THT]
  R20 = Resistor [tolerance=±5% resistance=33 package=THT]
  R21 = Resistor [tolerance=±5% resistance=33 package=THT]
  LED19 = LEDs [package=led10mm]
  LED20 = LEDs [package=led10mm]
  LED21 = LEDs [package=led10mm]
  LED22 = LEDs [package=led10mm]
  LED23 = LEDs [package=led10mm]
  LED24 = LEDs [package=led10mm]
  LED25 = LEDs [package=led10mm]
  LED26 = LEDs [package=led10mm]
  LED27 = LEDs [package=led10mm]
  R22 = Resistor [tolerance=±5% resistance=33 package=THT]
  R23 = Resistor [tolerance=±5% resistance=33 package=THT]
  R24 = Resistor [tolerance=±5% resistance=33 package=THT]
  LED28 = LEDs [package=led10mm]
  LED29 = LEDs [package=led10mm]
  LED30 = LEDs [package=led10mm]
  LED31 = LEDs [package=led10mm]
  LED32 = LEDs [package=led10mm]
  LED33 = LEDs [package=led10mm]
  LED34 = LEDs [package=led10mm]
  LED35 = LEDs [package=led10mm]
  LED36 = LEDs [package=led10mm]

nets:
  N1: IC2.A0, IC1.A0, J1.pin3, IC3.A0
  N2: IC2.A1, IC1.A1, J1.pin2, IC3.A1
  N3: IC2.A2, IC1.A2, J1.pin1, IC3.A2
  GND: IC2.CS2, IC2.GND, IC1.GND, IC3.CS2, IC3.CS3, IC3.GND, IC4.pin1, IC5.GND, R1.Pin_1, R2.Pin_1, IC6.pin1, IC7.GND, R6.Pin_1, R7.Pin_1
  N4: IC2.CS3, IC1.CS3, J2.pin1, IC3.CS1
  N5: IC2.CS1, IC1.CS2, J2.pin2
  5V: IC2.VCC, IC1.CS1, IC1.VCC, Q1.source, Q2.source, Q3.source, IC3.VCC, IC4.pin24, IC5.VDD, IC6.pin24, IC7.VDD, R11.Pin_0, R12.Pin_0, R13.Pin_0, R14.Pin_0, R15.Pin_0, R16.Pin_0, R17.Pin_0, R18.Pin_0
  N6: IC1.Y2, Q3.Gate
  N7: IC1.Y1, Q2.Gate
  N8: IC1.Y0, Q1.Gate
  N9: Q1.drain, LED1.A, LED2.A, LED3.A, LED10.A, LED12.A, LED15.A, LED25.A, LED26.A, LED27.A, LED34.A, LED35.A, LED36.A
  N10: Q2.drain, LED4.A, LED5.A, LED6.A, LED13.A, LED17.A, LED18.A, LED22.A, LED23.A, LED24.A, LED31.A, LED32.A, LED33.A
  N11: Q3.drain, LED7.A, LED8.A, LED9.A, LED11.A, LED14.A, LED16.A, LED19.A, LED20.A, LED21.A, LED28.A, LED29.A, LED30.A
  N12: IC4.pin2, J4.pin3, R12.Pin_1
  N13: IC4.pin3, IC5.CLK, J4.pin2, R13.Pin_1
  N14: IC4.pin4, IC5./LE, J4.pin1, R14.Pin_1
  N15: IC4.pin18, R5.Pin_1
  N16: IC4.pin19, R4.Pin_1
  N17: IC4.pin20, R3.Pin_1
  N18: IC4.pin21, IC5./OE, J4.pin4, R11.Pin_1
  N19: IC4.pin22, IC5.SDI
  N20: IC4.pin23, R1.Pin_0
  N21: IC5.OUT13, R19.Pin_1
  N22: IC5.OUT14, R20.Pin_1
  N23: IC5.OUT15, R21.Pin_1
  N24: IC5.R-EXT, R2.Pin_0
  N25: R3.Pin_0, LED2.C, LED6.C, LED7.C
  N26: R4.Pin_0, LED1.C, LED5.C, LED8.C
  N27: R5.Pin_0, LED3.C, LED4.C, LED9.C
  N28: IC6.pin2, J5.pin3, R16.Pin_1
  N29: IC6.pin3, J5.pin2, IC7.CLK, R17.Pin_1
  N30: IC6.pin4, J5.pin1, IC7./LE, R18.Pin_1
  N31: IC6.pin18, R9.Pin_1
  N32: IC6.pin19, R10.Pin_1
  N33: IC6.pin20, R8.Pin_1
  N34: IC6.pin21, J5.pin4, IC7./OE, R15.Pin_1
  N35: IC6.pin22, IC7.SDI
  N36: IC6.pin23, R6.Pin_0
  N37: IC7.OUT13, R22.Pin_1
  N38: IC7.OUT14, R23.Pin_1
  N39: IC7.OUT15, R24.Pin_1
  N40: IC7.R-EXT, R7.Pin_0
  N41: R8.Pin_0, LED12.C, LED13.C, LED16.C
  N42: R9.Pin_0, LED11.C, LED15.C, LED17.C
  N43: R10.Pin_0, LED10.C, LED14.C, LED18.C
  N44: R19.Pin_0, LED19.C, LED24.C, LED25.C
  N45: R20.Pin_0, LED20.C, LED23.C, LED27.C
  N46: R21.Pin_0, LED21.C, LED22.C, LED26.C
  N47: R22.Pin_0, LED28.C, LED33.C, LED34.C
  N48: R23.Pin_0, LED29.C, LED32.C, LED36.C
  N49: R24.Pin_0, LED30.C, LED31.C, LED35.C

custom parts:
  DIP - 24 pins: 16-BIT CONSTANT CURRENT LED SINK DRIVER
